# Fritzing sketch Sleep_coach_schematic_3up (saved by Fritzing 0.7.12b)
breadboards: 1

parts:
  U4 = atmega328 [package=dip]
  XTAL3 = Crystal [frequency="16 Mhz" package=THT]
  Power_plug3 = Power plug
  C10 = Ceramic Capacitor [capacitance=100nF package="100 mil [THT, multilayer]"]
  C11 = Electrolytic Capacitor [capacitance=10µF package="100 mil [THT, electrolytic]"]
  C12 = Ceramic Capacitor [capacitance=100nF package="100 mil [THT, multilayer]"]
  LED5 = LED - 5mm [color="Blue (525nm)" package="5 mm [THT]"]
  LED6 = LED - 5mm [color="Blue (525nm)" package="5 mm [THT]"]
  LED7 = LED - 5mm [color="Blue (525nm)" package="5 mm [THT]"]
  LED8 = LED - 5mm [color="Blue (525nm)" package="5 mm [THT]"]
  S2 = Pushbutton [package="[THT]"]
  R6 = Resistor [tolerance=±5% resistance=220 package=THT]
  R7 = Resistor [tolerance=±5% resistance=220 package=THT]
  R8 = Resistor [tolerance=±5% resistance=220 package=THT]
  R9 = Resistor [tolerance=±5% resistance=220 package=THT]
  R10 = Resistor [tolerance=±5% resistance=220 package=THT]
  J4 = female pin header, 1 pin [form="♀ (female)"]
  J5 = female pin header, 1 pin [form="♀ (female)"]
  J6 = female pin header, 1 pin [form="♀ (female)"]
  U5 = atmega328 [package=dip]
  XTAL4 = Crystal [frequency="16 Mhz" package=THT]
  Power_plug4 = Power plug
  C13 = Ceramic Capacitor [capacitance=100nF package="100 mil [THT, multilayer]"]
  C14 = Electrolytic Capacitor [capacitance=10µF package="100 mil [THT, electrolytic]"]
  C15 = Ceramic Capacitor [capacitance=100nF package="100 mil [THT, multilayer]"]
  LED9 = LED - 5mm [color="Blue (525nm)" package="5 mm [THT]"]
  LED10 = LED - 5mm [color="Blue (525nm)" package="5 mm [THT]"]
  LED11 = LED - 5mm [color="Blue (525nm)" package="5 mm [THT]"]
  LED12 = LED - 5mm [color="Blue (525nm)" package="5 mm [THT]"]
  S3 = Pushbutton [package="[THT]"]
  R11 = Resistor [tolerance=±5% resistance=220 package=THT]
  R12 = Resistor [tolerance=±5% resistance=220 package=THT]
  R13 = Resistor [tolerance=±5% resistance=220 package=THT]
  R14 = Resistor [tolerance=±5% resistance=220 package=THT]
  R15 = Resistor [tolerance=±5% resistance=220 package=THT]
  J7 = female pin header, 1 pin [form="♀ (female)"]
  J8 = female pin header, 1 pin [form="♀ (female)"]
  J9 = female pin header, 1 pin [form="♀ (female)"]
  U6 = atmega328 [package=dip]
  XTAL6 = Crystal [frequency="16 Mhz" package=THT]
  Power_plug6 = Power plug
  C17 = Ceramic Capacitor [capacitance=100nF package="100 mil [THT, multilayer]"]
  C18 = Electrolytic Capacitor [capacitance=10µF package="100 mil [THT, electrolytic]"]
  C20 = Ceramic Capacitor [capacitance=100nF package="100 mil [THT, multilayer]"]
  LED14 = LED - 5mm [color="Blue (525nm)" package="5 mm [THT]"]
  LED15 = LED - 5mm [color="Blue (525nm)" package="5 mm [THT]"]
  LED18 = LED - 5mm [color="Blue (525nm)" package="5 mm [THT]"]
  LED20 = LED - 5mm [color="Blue (525nm)" package="5 mm [THT]"]
  S5 = Pushbutton [package="[THT]"]
  R17 = Resistor [tolerance=±5% resistance=220 package=THT]
  R18 = Resistor [tolerance=±5% resistance=220 package=THT]
  R20 = Resistor [tolerance=±5% resistance=220 package=THT]
  R22 = Resistor [tolerance=±5% resistance=220 package=THT]
  R24 = Resistor [tolerance=±5% resistance=220 package=THT]
  J11 = female pin header, 1 pin [form="♀ (female)"]
  J13 = female pin header, 1 pin [form="♀ (female)"]
  J15 = female pin header, 1 pin [form="♀ (female)"]

nets:
  VCC: U4.VCC, U4.AVCC, U4.AREF, Power_plug3.VCC, C11.+, S2.Pin_1, S2.Pin_2
  GND: U4.GND, Power_plug3.GND, C10.0, C11.-, C12.0, R8.Pin_1, R9.Pin_1, R10.Pin_0, J5.pin1, J6.pin1
  N1: U4.XLAT1, XTAL3.pin_0, C12.1
  N2: U4.XLAT2, XTAL3.pin_1, C10.1
  N3: U4.D5_(PWM), R6.Pin_1
  N4: U4.D6_(PWM), R7.Pin_1
  N5: U4.D9_(PWM), LED6.anode
  N6: U4.D10_(PWM), LED5.anode
  N7: U4.D11_(PWM), S2.Pin_3, S2.Pin_4, R10.Pin_1
  N8: U4.A5, J4.pin1
  N9: LED5.cathode, R8.Pin_0
  N10: LED6.cathode, R9.Pin_0
  N11: LED7.cathode, LED8.cathode
  N12: LED7.anode, R7.Pin_0
  N13: LED8.anode, R6.Pin_0
  VCC_2: U5.VCC, U5.AVCC, U5.AREF, Power_plug4.VCC, C14.+, S3.Pin_1, S3.Pin_2
  GND_2: U5.GND, Power_plug4.GND, C13.0, C14.-, C15.0, R13.Pin_1, R14.Pin_1, R15.Pin_0, J8.pin1, J9.pin1
  N14: U5.XLAT1, XTAL4.pin_0, C15.1
  N15: U5.XLAT2, XTAL4.pin_1, C13.1
  N16: U5.D5_(PWM), R11.Pin_1
  N17: U5.D6_(PWM), R12.Pin_1
  N18: U5.D9_(PWM), LED10.anode
  N19: U5.D10_(PWM), LED9.anode
  N20: U5.D11_(PWM), S3.Pin_3, S3.Pin_4, R15.Pin_1
  N21: U5.A5, J7.pin1
  N22: LED9.cathode, R13.Pin_0
  N23: LED10.cathode, R14.Pin_0
  N24: LED11.cathode, LED12.cathode
  N25: LED11.anode, R12.Pin_0
  N26: LED12.anode, R11.Pin_0
  VCC_3: U6.VCC, U6.AVCC, U6.AREF, Power_plug6.VCC, C18.+, S5.Pin_1, S5.Pin_2
  GND_3: U6.GND, Power_plug6.GND, C17.0, C18.-, C20.0, R20.Pin_1, R22.Pin_1, R24.Pin_0, J13.pin1, J15.pin1
  N27: U6.XLAT1, XTAL6.pin_0, C20.1
  N28: U6.XLAT2, XTAL6.pin_1, C17.1
  N29: U6.D5_(PWM), R17.Pin_1
  N30: U6.D6_(PWM), R18.Pin_1
  N31: U6.D9_(PWM), LED15.anode
  N32: U6.D10_(PWM), LED14.anode
  N33: U6.D11_(PWM), S5.Pin_3, S5.Pin_4, R24.Pin_1
  N34: U6.A5, J11.pin1
  N35: LED14.cathode, R20.Pin_0
  N36: LED15.cathode, R22.Pin_0
  N37: LED18.cathode, LED20.cathode
  N38: LED18.anode, R18.Pin_0
  N39: LED20.anode, R17.Pin_0
